# Fritzing sketch nikon_lapse (saved by Fritzing 0.5.0b)
breadboards: 1

parts:
  Arduino1 = Arduino
  Stop_LED = green LED - 5mm [package="5 mm [THT]"]
  R2 = Resistor [resistance=560 package=THT]
  Third_LED = Red LED - 5mm [package="5 mm [THT]"]
  R2_2 = Resistor [resistance=560 package=THT]
  Control_Potentiometer = Rotary Potentiometer (Small)
  Infrared_LED = white LED - 5mm [package="5 mm [THT]"]

nets:
  N1: Arduino1.GND, R2.Pin_1, R2_2.Pin_1, Control_Potentiometer.leg1, Infrared_LED.cathode
  N2: Arduino1.D13, Infrared_LED.anode
  N3: Arduino1.D3, Third_LED.anode
  N4: Arduino1.D2, Stop_LED.anode
  N5: Arduino1.+5V, Control_Potentiometer.leg2
  N6: Arduino1.A0, Control_Potentiometer.wiper
  N7: Stop_LED.cathode, R2.Pin_0
  N8: Third_LED.cathode, R2_2.Pin_0
